# Fritzing sketch 4th lpf ケース内配線 (saved by Fritzing 0.9.2b)
perfboards: 2

parts:
  J1 = female pin header, 3 pins [form="♀ (female)"]
  J2 = female pin header, 2 pins [form="♀ (female)"]
  J3 = female pin header, 3 pins [form="♀ (female)"]
  J4 = female pin header, 3 pins [form="♀ (female)"]
  J5 = female pin header, 2 pins [form="♀ (female)"]
  Power_plug1 = Power plug
  S1 = Toggle Switch [package=THT]
  TRS1 = Audio Jack (TRS) 3.5mm [package="4Ucon 08780 [THT]"]
  TRS2 = Audio Jack (TRS) 3.5mm [package="4Ucon 08780 [THT]"]
  S2 = Toggle Switch [package=THT]
  R1 = Rotary Potentiometer (Small) [maximum_resistance=100kΩ package=THT]

nets:
  N1: J1.pin1, TRS2.Sleeve
  N2: J1.pin2, TRS2.Ring
  N3: J1.pin3, TRS2.Tip
  N4: J2.pin1, TRS1.Sleeve, R1.leg1
  N5: J2.pin2, R1.wiper
  N6: J3.pin1, J4.pin2
  N7: J3.pin2, J4.pin3
  N8: J3.pin3, J4.pin1
  N9: J5.pin1, Power_plug1.GND
  N10: J5.pin2, S1.COM
  N11: Power_plug1.VCC, S1.L1
  N12: TRS1.Ring, S2.L2
  N13: TRS1.Tip, S2.L1
  N14: S2.COM, R1.leg2

notes:
  LPF
  Rail
  Splitter
  Input
  Output
  T: Filtered
  R: Bypass
  S:GND
  Level
  Input Select
  Power
  Power
  Switch
